// Digital circuit basic_op_sw2_7seg.dig as structural Verilog
module basic_op_sw2_7seg (
  input  SW0,
  input  SW1,
  input  SW2,
  input  SW3,
  input  SW4,
  input  SW5,
  input  SW6,
  input  SW7,
  input  SW8,
  input  SW9,
  input  SW10,
  input  SW11,
  input  SW12,
  input  SW13,
  input  SW14,
  input  SW15,
  input  BTN0,
  input  clk,
  input  BTN1,
  input  BTN3,
  input  BTN2,
  output LD0,
  output LD1,
  output LD2,
  output LD3,
  output LE4,
  output LD5,
  output LD6,
  output LD7,
  output LD8,
  output LD9,
  output LD10,
  output LD11,
  output LD12,
  output LD13,
  output LD14,
  output LD15,
  output RGB0R,
  output RGB0G,
  output RGB0B,
  output RGB1R,
  output RGB1G,
  output RGB1B,
  output D0AN3,
  output D0AN2,
  output D0AN1,
  output D0AN0,
  output D0SEG3,
  output D0SEG2,
  output D0SEG1,
  output D0SEG0,
  output D0SEG4,
  output D0SEG5,
  output D0SEG6,
  output D0SEG7,
  output D1AN3,
  output D1AN2,
  output D1AN1,
  output D1AN0,
  output D1SEG3,
  output D1SEG2,
  output D1SEG1,
  output D1SEG0,
  output D1SEG4,
  output D1SEG5,
  output D1SEG6,
  output D1SEG7
);

  wire and_1_out, and_2_out, not_1_out;
  wire [1:0] clkdiv_out_2;
  wire [3:0] L7segFF_q, L7segFF_q_2, L7segFF_q_3, L7segFF_q_4, multiplexer_1_out, multiplexer_2_out,
       R7segFF_q, R7segFF_q_2, R7segFF_q_3, R7segFF_q_4;
  wire [4:0] ctrb0_out, ctrb1_out, ctrg0_out, ctrg1_out, ctrr0_out, cttr1_out, Db0_q, Db1_q, Dg0_q, Dg1_q,
       Dr0_q, Dr1_q;
  wire [11:0] clkdiv_out;

  not not_1 (not_1_out, SW15);
  and and_1 (and_1_out, not_1_out, BTN1);
  and and_2 (and_2_out, SW15, BTN1);
  Register #(.Bits(5)) Dr0 (.D({SW4, SW3, SW2, SW1, SW0}), .C(clk), .en(and_1_out), .Q(Dr0_q));
  Register #(.Bits(5)) Dr1 (.D({SW4, SW3, SW2, SW1, SW0}), .C(clk), .en(and_2_out), .Q(Dr1_q));
  Register #(.Bits(5)) Dg0 (.D({SW9, SW8, SW7, SW6, SW5}), .C(clk), .en(and_1_out), .Q(Dg0_q));
  Register #(.Bits(5)) Dg1 (.D({SW9, SW8, SW7, SW6, SW5}), .C(clk), .en(and_2_out), .Q(Dg1_q));
  Register #(.Bits(5)) Db0 (.D({SW14, SW13, SW12, SW11, SW10}), .C(clk), .en(and_1_out), .Q(Db0_q));
  Register #(.Bits(5)) Db1 (.D({SW14, SW13, SW12, SW11, SW10}), .C(clk), .en(and_2_out), .Q(Db1_q));
  Comparator #(.Bits(5)) comparator_1 (.a(ctrr0_out), .b(Dr0_q), .lt(RGB0R));  // open: gt, eq
  Comparator #(.Bits(5)) comparator_2 (.a(cttr1_out), .b(Dr1_q), .lt(RGB1R));  // open: gt, eq
  Comparator #(.Bits(5)) comparator_3 (.a(ctrg0_out), .b(Dg0_q), .lt(RGB0G));  // open: gt, eq
  Comparator #(.Bits(5)) comparator_4 (.a(ctrg1_out), .b(Dg1_q), .lt(RGB1G));  // open: gt, eq
  Comparator #(.Bits(5)) comparator_5 (.a(ctrb0_out), .b(Db0_q), .lt(RGB0B));  // open: gt, eq
  Comparator #(.Bits(5)) comparator_6 (.a(ctrb1_out), .b(Db1_q), .lt(RGB1B));  // open: gt, eq
  Counter #(.Bits(5)) ctrr0 (.en(1'b1), .C(clk), .clr(1'b0), .out(ctrr0_out));  // open: ovf
  Counter #(.Bits(5)) cttr1 (.en(1'b1), .C(clk), .clr(1'b0), .out(cttr1_out));  // open: ovf
  Counter #(.Bits(5)) ctrg0 (.en(1'b1), .C(clk), .clr(1'b0), .out(ctrg0_out));  // open: ovf
  Counter #(.Bits(5)) ctrg1 (.en(1'b1), .C(clk), .clr(1'b0), .out(ctrg1_out));  // open: ovf
  Counter #(.Bits(5)) ctrb0 (.en(1'b1), .C(clk), .clr(1'b0), .out(ctrb0_out));  // open: ovf
  Counter #(.Bits(5)) ctrb1 (.en(1'b1), .C(clk), .clr(1'b0), .out(ctrb1_out));  // open: ovf
  Register #(.Bits(16)) Dff (
    .D({SW15, SW14, SW13, SW12, SW11, SW10, SW9, SW8, SW7, SW6, SW5, SW4, SW3, SW2, SW1, SW0}), .C(clk),
    .en(BTN0), .Q({LD15, LD14, LD13, LD12, LD11, LD10, LD9, LD8, LD7, LD6, LD5, LE4, LD3, LD2, LD1, LD0}));
  Counter #(.Bits(12)) clkdiv (
    .en(1'b1), .C(clk), .clr(1'b0), .out({clkdiv_out[11], clkdiv_out_2, clkdiv_out[8:0]}));  // open: ovf
  Register #(.Bits(16)) L7segFF (
    .D({SW15, SW14, SW13, SW12, SW11, SW10, SW9, SW8, SW7, SW6, SW5, SW4, SW3, SW2, SW1, SW0}), .C(clk),
    .en(BTN2), .Q({L7segFF_q_4, L7segFF_q_3, L7segFF_q_2, L7segFF_q}));
  Register #(.Bits(16)) R7segFF (
    .D({SW15, SW14, SW13, SW12, SW11, SW10, SW9, SW8, SW7, SW6, SW5, SW4, SW3, SW2, SW1, SW0}), .C(clk),
    .en(BTN3), .Q({R7segFF_q_4, R7segFF_q_3, R7segFF_q_2, R7segFF_q}));
  Multiplexer #(.Selector_Bits(2), .Bits(4)) multiplexer_1 (
    .sel(clkdiv_out_2), .in_0(R7segFF_q), .in_1(R7segFF_q_2), .in_2(R7segFF_q_3), .in_3(R7segFF_q_4),
    .out(multiplexer_1_out));
  Multiplexer #(.Selector_Bits(2), .Bits(4)) multiplexer_2 (
    .sel(clkdiv_out_2), .in_0(L7segFF_q), .in_1(L7segFF_q_2), .in_2(L7segFF_q_3), .in_3(L7segFF_q_4),
    .out(multiplexer_2_out));
  ROM #(.AddrBits(4), .Bits(7)) hexdecode (
    .A(multiplexer_1_out), .sel(1'b1), .D({D1SEG6, D1SEG5, D1SEG4, D1SEG3, D1SEG2, D1SEG1, D1SEG0}));
  ROM #(.AddrBits(4), .Bits(7)) hexdecode_2 (
    .A(multiplexer_2_out), .sel(1'b1), .D({D0SEG6, D0SEG5, D0SEG4, D0SEG3, D0SEG2, D0SEG1, D0SEG0}));
  Demultiplexer #(.Selector_Bits(2), .Default(1)) demultiplexer_1 (
    .sel(clkdiv_out_2), .in(1'b0), .out_0(D0AN0), .out_1(D0AN1), .out_2(D0AN2), .out_3(D0AN3));
  Demultiplexer #(.Selector_Bits(2), .Default(1)) demultiplexer_2 (
    .sel(clkdiv_out_2), .in(1'b0), .out_0(D1AN0), .out_1(D1AN1), .out_2(D1AN2), .out_3(D1AN3));

  assign D0SEG7 = 1'b1;
  assign D1SEG7 = 1'b1;

  // Notes on the sheet:
  //   SW0: pin V2
  //   SW1: pin U2
  //   SW2: pin U1
  //   SW3: pin T2
  //   SW4: pin T1
  //   SW5: pin R2
  //   SW6: pin R1
  //   SW7: pin P2
  //   SW8: pin P1
  //   SW9: pin N2
  //   SW10: pin N1
  //   SW11: pin M2
  //   SW12: pin M1
  //   SW13: pin L1
  //   SW14: pin K2
  //   SW15: pin K1
  //   LD0: pin G1
  //   LD1: pin G2
  //   LD2: pin F1
  //   LD3: pin F2
  //   LE4: pin E1
  //   LD5: pin E2
  //   LD6: pin E3
  //   LD7: pin E5
  //   LD8: pin E6
  //   LD9: pin C3
  //   LD10: pin B2
  //   LD11: pin A2
  //   LD12: pin B3
  //   LD13: pin A3
  //   LD14: pin B4
  //   LD15: pin A4
  //   BTN0: pin J2
  //   clk: pin F14, Hz: 2147483647
  //   BTN1: pin J5
  //   RGB0R: pin V6
  //   RGB0G: pin V4
  //   RGB0B: pin U6
  //   RGB1R: pin U3
  //   RGB1G: pin V3
  //   RGB1B: pin V5
  //   BTN3: pin J1
  //   BTN2: pin H2
  //   D0AN3: pin A8
  //   D0AN2: pin C7
  //   D0AN1: pin C4
  //   D0AN0: pin D5
  //   D0SEG3: pin B7
  //   D0SEG2: pin A5
  //   D0SEG1: pin C5
  //   D0SEG0: pin D7
  //   D0SEG4: pin A7
  //   D0SEG5: pin D6
  //   D0SEG6: pin B5
  //   D0SEG7: pin A6
  //   D1AN3: pin E4
  //   D1AN2: pin F3
  //   D1AN1: pin J4
  //   D1AN0: pin H3
  //   D1SEG3: pin C2
  //   D1SEG2: pin D2
  //   D1SEG1: pin J3
  //   D1SEG0: pin F4
  //   D1SEG4: pin B1
  //   D1SEG5: pin H4
  //   D1SEG6: pin D1
  //   D1SEG7: pin C1
  //   RGB led0
  //   RGB led1
  //   Switches
  //   LED's
  //   Right Seven Segment Display
  //   is active low
  //   contents of hexdecode (hex, n*v repeats v):
  //   3f40,1879,36a4,3cb0,1999,12,2,78,0,10,8,3,46,186a1,18006,e
  //   contents of hexdecode_2 (hex, n*v repeats v):
  //   3f40,1879,36a4,3cb0,1999,12,2,78,0,10,8,3,46,186a1,18006,e
  //   Left Seven Segment Display
  //   Is active low
  //   Left Seven Segment Display
  //   is active low
endmodule
